# Fritzing sketch NodeMCUV3 (saved by Fritzing 0.9.3b)
circuit board: 8.46667cm x 5.64444cm
perfboards: 1

parts:
  Power_plug1 = Power plug
  Power_plug2 = Power plug  # not connected
  U1 = NodeMCU V3.0
  Componente1 = SRF05 Ultrasonic Rangefinder
  RHT1 = Humidity and Temperature Sensor RHT03
  LED1 = LED - 3mm [color="Red (633nm)" package="3 mm [THT]"]
  R1 = Resistor [tolerance=±5% resistance=220 package="0603 [SMD]"]
  KY-1 = Keyes Relay [package=THT]
  KY-2 = Keyes Relay [package=THT]
  R2 = Resistor [tolerance=±5% resistance=10k package="0603 [SMD]"]

nets:
  GND: Power_plug1.GND, U1.GND#6, U1.GND#13, U1.GND#16, U1.GND#33, Componente1.GND, RHT1.GND_2, LED1.cathode, KY-1.ground, KY-2.ground
  VCC: Power_plug1.VCC, U1.Vin, Componente1.VCC, RHT1.Vcc, KY-1.power, KY-2.power, R2.Pin_0
  N1: U1.D1, Componente1.Trig
  N2: U1.D2, Componente1.Echo
  N3: U1.D3, RHT1.Data-signal, R2.Pin_1
  N4: U1.D4, R1.Pin_0
  N5: U1.D5, KY-1.signal
  N6: U1.D6, KY-2.signal
  N7: LED1.anode, R1.Pin_1

custom parts:
  NodeMCU V3.0: ESP8266 based NodeMCU
  Keyes Relay: The Keyes 5V relay module is suitable for SCM development, home appliance control. It uses a 5V~12V TIL control signal which can control DC / AC signal.
